// Logisim project piped.circ as structural Verilog: 7 circuits, main circuit main
module main (
);

  wire and_1_out, Clock, ex_mem_1_zero_read, mips_alu_1_p1, mips_alu_1_p6, mips_alu_1_p8, mips_ram_1_p3,
       mips_ram_1_p5, mips_ram_1_p9, registerfile_1_p2, registerfile_1_p6;
  wire [1:0] mips_alu_1_p2;
  wire [3:0] mips_alu_1_p5;
  wire [4:0] ex_mem_1_write_register_read, id_ex_1_write_register_read, instructiondecode_1__11_15,
       instructiondecode_1__16_20, instructiondecode_1__21_25, multiplexer_2_out, registerfile_1_p4;
  wire [15:0] instructiondecode_1__0_15;
  wire [31:0] adder_1_out, adder_2_out, bit_extender_1_out, ex_mem_1_branch_address_read, ex_mem_1_out_10,
       ex_mem_1_register_read_data_2_read, id_ex_1_immediate_field_write_2, id_ex_1_incremented_pc_read,
       id_ex_1_register_read_data_1_write_2, id_ex_1_register_read_data_2_read, if_id_1_out_4, if_id_1_out_5,
       mem_wb_1_alu_result_read, mem_wb_1_read_data_write_2, mips_alu_1_p7, mips_ram_1_p8,
       mipsprogramrom_1_p2, mipsprogramrom_1_p3, multiplexer_1_out, multiplexer_3_out, PC_q,
       registerfile_1_p8, registerfile_1_p9, shifter_1_out;

  Clock clock_1 (.out(Clock));
  Multiplexer #(.width(32), .enable("false")) multiplexer_1 (
    .in0(adder_1_out), .in1(ex_mem_1_branch_address_read), .out(multiplexer_1_out), .sel(and_1_out));
  Register #(.width(32)) PC (.D(multiplexer_1_out), .Q(PC_q), .clk(Clock));  // open: en, clr
  Adder #(.width(32)) adder_1 (.a(PC_q), .b(32'h4), .out(adder_1_out));  // open: cin, cout
  // MIPSProgramROM mipsprogramrom_1: pin names not known; wires that end beside it: PC_q, mipsprogramrom_1_p2, mipsprogramrom_1_p3
  IF_ID if_id_1 (
    .in_1(adder_1_out), .in_2(mipsprogramrom_1_p2), .out_4(if_id_1_out_4), .out_5(if_id_1_out_5),
    .Clock(Clock));
  instructionDecode instructiondecode_1 (
    ._32_bit_instruction(if_id_1_out_5), ._21_25(instructiondecode_1__21_25),
    ._16_20(instructiondecode_1__16_20), ._11_15(instructiondecode_1__11_15),
    ._0_15(instructiondecode_1__0_15));  // open: _26_31, _0_5
  Multiplexer #(.width(5), .enable("false")) multiplexer_2 (
    .in0(instructiondecode_1__16_20), .in1(instructiondecode_1__11_15), .out(multiplexer_2_out),
    .sel(registerfile_1_p6));
  // RegisterFile registerfile_1: pin names not known; wires that end beside it: Clock, registerfile_1_p2, registerfile_1_p2, registerfile_1_p4, instructiondecode_1__21_25, registerfile_1_p6, instructiondecode_1__16_20, registerfile_1_p8, registerfile_1_p9
  assign bit_extender_1_out = {{16{instructiondecode_1__0_15[15]}}, instructiondecode_1__0_15};  // Bit_Extender bit_extender_1
  ID_EX id_ex_1 (
    .Incremented_PC_write(if_id_1_out_4), .Register_read_data_1_write(registerfile_1_p8),
    .Register_read_data_2_write(registerfile_1_p9), .Immediate_field_write(bit_extender_1_out),
    .Incremented_PC_read(id_ex_1_incremented_pc_read),
    .Register_read_data_1_write_2(id_ex_1_register_read_data_1_write_2),
    .Register_read_data_2_read(id_ex_1_register_read_data_2_read),
    .Immediate_field_write_2(id_ex_1_immediate_field_write_2), .Write_register_write(multiplexer_2_out),
    .Write_register_read(id_ex_1_write_register_read), .Clock(Clock));
  Shifter #(.width(32)) shifter_1 (.in(id_ex_1_immediate_field_write_2), .\dist (5'b00010), .out(shifter_1_out));
  Multiplexer #(.width(32), .enable("false")) multiplexer_3 (
    .in0(id_ex_1_register_read_data_2_read), .in1(id_ex_1_immediate_field_write_2), .out(multiplexer_3_out),
    .sel(mips_alu_1_p1));
  Adder #(.width(32)) adder_2 (
    .a(id_ex_1_incremented_pc_read), .b(shifter_1_out), .out(adder_2_out));  // open: cin, cout
  // MIPS_ALU mips_alu_1: pin names not known; wires that end beside it: mips_alu_1_p1, mips_alu_1_p2, id_ex_1_register_read_data_1_write_2, multiplexer_3_out, mips_alu_1_p5, mips_alu_1_p6, mips_alu_1_p7, mips_alu_1_p8
  ALU_control alu_control_1 (
    .Funct_field(id_ex_1_immediate_field_write_2[5:0]), .ALUOp(mips_alu_1_p2), .out_3(mips_alu_1_p5));
  EX_MEM ex_mem_1 (
    .Branch_address_write(adder_2_out), .Zero_write(mips_alu_1_p6),
    .Register_read_data_2_write(mips_alu_1_p7), .in_4(id_ex_1_register_read_data_2_read), .Clock(Clock),
    .Branch_address_read(ex_mem_1_branch_address_read), .Zero_read(ex_mem_1_zero_read),
    .Register_read_data_2_read(ex_mem_1_register_read_data_2_read), .out_10(ex_mem_1_out_10),
    .Write_register_write(id_ex_1_write_register_read), .Write_register_read(ex_mem_1_write_register_read));
  and and_1 (and_1_out, mips_alu_1_p8, ex_mem_1_zero_read);
  // MIPS_RAM mips_ram_1: pin names not known; wires that end beside it: ex_mem_1_register_read_data_2_read, ex_mem_1_out_10, mips_ram_1_p3, mips_ram_1_p3, mips_ram_1_p5, mips_ram_1_p5, Clock, mips_ram_1_p8, mips_ram_1_p9
  MEM_WB mem_wb_1 (
    .Read_data_write(mips_ram_1_p8), .ALU_result_write(ex_mem_1_register_read_data_2_read),
    .Read_data_write_2(mem_wb_1_read_data_write_2), .ALU_result_read(mem_wb_1_alu_result_read),
    .Write_register_read(registerfile_1_p4), .Write_register_write(ex_mem_1_write_register_read),
    .Clock(Clock));
  Multiplexer #(.width(32), .enable("false")) multiplexer_4 (
    .in0(mem_wb_1_read_data_write_2), .in1(mem_wb_1_alu_result_read), .out(mipsprogramrom_1_p3),
    .sel(mips_ram_1_p9));
endmodule

module IF_ID (
  input  [31:0] in_1,
  input  [31:0] in_2,
  input  Clock,
  output [31:0] out_4,
  output [31:0] out_5
);

  Register #(.width(32)) Incremented_PC (.D(in_1), .Q(out_4), .clk(Clock));  // open: en, clr
  Register #(.width(32)) Fetched_instruction (.D(in_2), .Q(out_5), .clk(Clock));  // open: en, clr
endmodule

module ID_EX (
  input  [31:0] Incremented_PC_write,
  input  [31:0] Register_read_data_1_write,
  input  [31:0] Register_read_data_2_write,
  input  [31:0] Immediate_field_write,
  input  [4:0] Write_register_write,
  input  Clock,
  output [31:0] Incremented_PC_read,
  output [31:0] Register_read_data_1_write_2,
  output [31:0] Register_read_data_2_read,
  output [31:0] Immediate_field_write_2,
  output [4:0] Write_register_read
);

  Register #(.width(32)) Incremented_PC (
    .D(Incremented_PC_write), .Q(Incremented_PC_read), .clk(Clock));  // open: en, clr
  Register #(.width(32)) Register_read_data_1 (
    .D(Register_read_data_1_write), .Q(Register_read_data_1_write_2), .clk(Clock));  // open: en, clr
  Register #(.width(32)) Register_read_data_2 (
    .D(Register_read_data_2_write), .Q(Register_read_data_2_read), .clk(Clock));  // open: en, clr
  Register #(.width(32)) Immediate_field (
    .D(Immediate_field_write), .Q(Immediate_field_write_2), .clk(Clock));  // open: en, clr
  Register #(.width(5)) Write_register (
    .D(Write_register_write), .Q(Write_register_read), .clk(Clock));  // open: en, clr
endmodule

module instructionDecode (
  input  [31:0] _32_bit_instruction,
  output [5:0] _26_31,
  output [4:0] _21_25,
  output [4:0] _16_20,
  output [15:0] _0_15,
  output [4:0] _11_15,
  output [5:0] _0_5
);


  assign _0_5 = _32_bit_instruction[5:0];
  assign _0_15 = _32_bit_instruction[15:0];
  assign _11_15 = _32_bit_instruction[15:11];
  assign _16_20 = _32_bit_instruction[20:16];
  assign _21_25 = _32_bit_instruction[25:21];
  assign _26_31 = _32_bit_instruction[31:26];
endmodule

module EX_MEM (
  input  [31:0] Branch_address_write,
  input  Zero_write,
  input  [31:0] Register_read_data_2_write,
  input  [31:0] in_4,
  input  [4:0] Write_register_write,
  input  Clock,
  output [31:0] Branch_address_read,
  output Zero_read,
  output [31:0] Register_read_data_2_read,
  output [31:0] out_10,
  output [4:0] Write_register_read
);

  Register #(.width(32)) Branch_address (
    .D(Branch_address_write), .Q(Branch_address_read), .clk(Clock));  // open: en, clr
  Register #(.width(1)) Zero (.D(Zero_write), .Q(Zero_read), .clk(Clock));  // open: en, clr
  Register #(.width(32)) Register_read_data_2 (
    .D(Register_read_data_2_write), .Q(Register_read_data_2_read), .clk(Clock));  // open: en, clr
  Register #(.width(32)) register_1 (.D(in_4), .Q(out_10), .clk(Clock));  // open: en, clr
  Register #(.width(5)) Write_register (
    .D(Write_register_write), .Q(Write_register_read), .clk(Clock));  // open: en, clr
endmodule

module MEM_WB (
  input  [31:0] Read_data_write,
  input  [31:0] ALU_result_write,
  input  [4:0] Write_register_write,
  input  Clock,
  output [31:0] Read_data_write_2,
  output [31:0] ALU_result_read,
  output [4:0] Write_register_read
);

  Register #(.width(32)) Read_data (.D(Read_data_write), .Q(Read_data_write_2), .clk(Clock));  // open: en, clr
  Register #(.width(32)) ALU_result (.D(ALU_result_write), .Q(ALU_result_read), .clk(Clock));  // open: en, clr
  Register #(.width(5)) Write_register (
    .D(Write_register_write), .Q(Write_register_read), .clk(Clock));  // open: en, clr
endmodule

module ALU_control (
  input  [5:0] Funct_field,
  input  [1:0] ALUOp,
  output [3:0] out_3
);

  wire [7:0] adder_1_out, bit_extender_1_out, bit_extender_2_out, shifter_1_out;

  assign bit_extender_1_out = {{6{1'b0}}, ALUOp};  // Bit_Extender bit_extender_1
  assign bit_extender_2_out = {{2{1'b0}}, Funct_field};  // Bit_Extender bit_extender_2
  Shifter shifter_1 (.in(bit_extender_1_out), .\dist (3'b110), .out(shifter_1_out));
  Adder adder_1 (.a(bit_extender_2_out), .b(shifter_1_out), .out(adder_1_out));  // open: cin, cout
  // PLA pla_1: pin names not known; wires that end beside it: adder_1_out, out_3
endmodule
